# Fritzing sketch A330_FCU (saved by Fritzing 0.9.3b)

parts:
  SPDM = LED - 3mm [color="Orange (612nm)" package="3 mm [THT]"]  # not connected
  HDGM = LED - 3mm [color="Orange (612nm)" package="3 mm [THT]"]  # not connected
  LVL/CH = LED - 3mm [color="Orange (612nm)" package="3 mm [THT]"]  # not connected
  IC1 = IC, DIP package, 28 pins [chip_label=MCP23017]
  HDGSEL = Rotary Encoder [package=THT]  # not connected
  switch1 = Rotary_Switch_12x1  # not connected
  SPDSEL = Rotary Encoder [package=THT]  # not connected
  ALTSEL = Rotary Encoder [package=THT]  # not connected
  V/SSEL = Rotary Encoder [package=THT]  # not connected
  IC2 = IC, DIP package, 28 pins [chip_label=MCP23017]
  IC3 = IC, DIP package, 28 pins [chip_label=MCP23017]
  IC4 = IC, DIP package, 24 pins [chip_label=MAX7219]
  IC5 = IC, DIP package, 24 pins [chip_label=MAX7219]
  SPD3 = 7 Segment Display
  SPD2 = 7 Segment Display
  HDG1 = 7 Segment Display
  HDG2 = 7 Segment Display
  HDG3 = 7 Segment Display
  ALT1 = 7 Segment Display
  ALT2 = 7 Segment Display
  ALT3 = 7 Segment Display
  ALT4 = 7 Segment Display
  ALT5 = 7 Segment Display
  V/S1 = 7 Segment Display
  V/S2 = 7 Segment Display
  V/S3 = 7 Segment Display
  V/S4 = 7 Segment Display
  V/S5 = 7 Segment Display
  SPD1 = 7 Segment Display
  WeMos_D1_Mini = WeMos D1 Mini
  S1 = Pushbutton [package="[THT]"]  # not connected
  LED1 = LED - 3mm [color="Green (560nm)" package="3 mm [THT]"]  # not connected
  R2 = Resistor [tolerance=±5% resistance=10k package=THT]
  R1 = Resistor [tolerance=±5% resistance=10k package=THT]
  C1 = Ceramic Capacitor [capacitance=0.1µF part_number=IC4 package="100 mil [THT, multilayer]"]
  C2 = Ceramic Capacitor [capacitance=0.1µF part_number=IC5 package="100 mil [THT, multilayer]"]
  Bauteil1 = Logic Level Converter

nets:
  SCL: IC1.pin12, IC2.pin12, IC3.pin12, WeMos_D1_Mini.D1
  SDA: IC1.pin13, IC2.pin13, IC3.pin13, WeMos_D1_Mini.D2
  MOSI: IC4.pin1, WeMos_D1_Mini.D7
  N1: IC4.pin2, SPD1.common_cathode
  N2: IC4.pin3, HDG2.common_cathode
  GND: IC4.pin4, IC4.pin9, IC5.pin4, IC5.pin9, WeMos_D1_Mini.G, C1.0, C2.0, Bauteil1.GND
  N3: IC4.pin5, ALT1.common_cathode
  N4: IC4.pin6, SPD3.common_cathode
  N5: IC4.pin7, HDG1.common_cathode
  N6: IC4.pin8, ALT2.common_cathode
  N7: IC4.pin10, HDG3.common_cathode
  N8: IC4.pin11, SPD2.common_cathode
  CS: IC4.pin12, IC5.pin12, WeMos_D1_Mini.D8
  CLK: IC4.pin13, IC5.pin13, WeMos_D1_Mini.D5
  N9: IC4.pin14, SPD3.Segment_A, SPD2.Segment_A, HDG1.Segment_A, HDG2.Segment_A, HDG3.Segment_A, ALT1.Segment_A, ALT2.Segment_A, SPD1.Segment_A
  N10: IC4.pin15, SPD3.Segment_F, SPD2.Segment_F, HDG1.Segment_F, HDG2.Segment_F, HDG3.Segment_F, ALT1.Segment_F, ALT2.Segment_F, SPD1.Segment_F
  N11: IC4.pin16, SPD3.Segment_B, SPD2.Segment_B, HDG1.Segment_B, HDG2.Segment_B, HDG3.Segment_B, ALT1.Segment_B, ALT2.Segment_B, SPD1.Segment_B
  N12: IC4.pin17, SPD3.Segment_G, SPD2.Segment_G, HDG1.Segment_G, HDG2.Segment_G, HDG3.Segment_G, ALT1.Segment_G, ALT2.Segment_G, SPD1.Segment_G
  N13: IC4.pin18, R1.Pin_0
  5V: IC4.pin19, IC5.pin19, WeMos_D1_Mini.5V, R2.Pin_1, R1.Pin_1, C1.1, C2.1, Bauteil1.HV
  N14: IC4.pin20, SPD3.Segment_C, SPD2.Segment_C, HDG1.Segment_C, HDG2.Segment_C, HDG3.Segment_C, ALT1.Segment_C, ALT2.Segment_C, SPD1.Segment_C
  N15: IC4.pin21, SPD3.Segment_E, SPD2.Segment_E, HDG1.Segment_E, HDG2.Segment_E, HDG3.Segment_E, ALT1.Segment_E, ALT2.Segment_E, SPD1.Segment_E
  N16: IC4.pin22, SPD3.Segment_DP, SPD2.Segment_DP, HDG1.Segment_DP, HDG2.Segment_DP, HDG3.Segment_DP, ALT1.Segment_DP, ALT2.Segment_DP, SPD1.Segment_DP
  N17: IC4.pin23, SPD3.Segment_D, SPD2.Segment_D, HDG1.Segment_D, HDG2.Segment_D, HDG3.Segment_D, ALT1.Segment_D, ALT2.Segment_D, SPD1.Segment_D
  N18: IC4.pin24, IC5.pin1
  N19: IC5.pin2, ALT3.common_cathode
  N20: IC5.pin3, V/S2.common_cathode
  N21: IC5.pin5, V/S4.common_cathode
  N22: IC5.pin6, ALT5.common_cathode
  N23: IC5.pin7, V/S1.common_cathode
  N24: IC5.pin8, V/S5.common_cathode
  N25: IC5.pin10, V/S3.common_cathode
  N26: IC5.pin11, ALT4.common_cathode
  N27: IC5.pin14, ALT3.Segment_A, ALT4.Segment_A, ALT5.Segment_A, V/S1.Segment_A, V/S2.Segment_A, V/S3.Segment_A, V/S4.Segment_A, V/S5.Segment_A
  N28: IC5.pin15, ALT3.Segment_F, ALT4.Segment_F, ALT5.Segment_F, V/S1.Segment_F, V/S2.Segment_F, V/S3.Segment_F, V/S4.Segment_F, V/S5.Segment_F
  N29: IC5.pin16, ALT3.Segment_B, ALT4.Segment_B, ALT5.Segment_B, V/S1.Segment_B, V/S2.Segment_B, V/S3.Segment_B, V/S4.Segment_B, V/S5.Segment_B
  N30: IC5.pin17, ALT3.Segment_G, ALT4.Segment_G, ALT5.Segment_G, V/S1.Segment_G, V/S2.Segment_G, V/S3.Segment_G, V/S4.Segment_G, V/S5.Segment_G
  N31: IC5.pin18, R2.Pin_0
  N32: IC5.pin20, ALT3.Segment_C, ALT4.Segment_C, ALT5.Segment_C, V/S1.Segment_C, V/S2.Segment_C, V/S3.Segment_C, V/S4.Segment_C, V/S5.Segment_C
  N33: IC5.pin21, ALT3.Segment_E, ALT4.Segment_E, ALT5.Segment_E, V/S1.Segment_E, V/S2.Segment_E, V/S3.Segment_E, V/S4.Segment_E, V/S5.Segment_E
  N34: IC5.pin22, ALT3.Segment_DP, ALT4.Segment_DP, ALT5.Segment_DP, V/S1.Segment_DP, V/S2.Segment_DP, V/S3.Segment_DP, V/S4.Segment_DP, V/S5.Segment_DP
  N35: IC5.pin23, ALT3.Segment_D, ALT4.Segment_D, ALT5.Segment_D, V/S1.Segment_D, V/S2.Segment_D, V/S3.Segment_D, V/S4.Segment_D, V/S5.Segment_D
  3.3V: WeMos_D1_Mini.3V3, Bauteil1.LV
  MISO: WeMos_D1_Mini.D6
